# Fritzing sketch electrical_scheme (saved by Fritzing 0.9.3b)
circuit board: 8.46667cm x 5.64444cm
breadboards: 1
perfboards: 1

parts:
  Raspberry_Pi2 = Raspberry Pi B rev2
  Part3 = Soil Moisture Sensor
  Part4 = Soil Moisture Sensor  # not connected
  LED5 = LED - 5mm [color="Green (565nm)" package="5 mm [THT]"]
  LED7 = LED - 5mm [color="Red (633nm)" package="5 mm [THT]"]
  WeMos_D1_Mini_Relay_Shield1 = WeMos D1 Mini Relay Shield
  BAT3 = BC9VPC [package=bc9vpc]
  R7 = Resistor [tolerance=±5% resistance=680 package=THT]
  S6 = Taiway 100-SP-X-T1 SPDT Miniature Toggle Switch [part_number=100-SP-X-T1-0-0-B1-M2 package=THT]
  M2 = DC Motor [part_number=Pompa]
  R11 = Resistor [tolerance=±5% resistance=680 package=THT]
  R15 = Resistor [tolerance=±5% resistance=680 package=THT]
  LED6 = LED - 5mm [color="Yellow (592nm)" package="5 mm [THT]"]
  WeMos_D1_Mini_Relay_Shield2 = WeMos D1 Mini Relay Shield
  U1 = M10X2 [package=2x10_lock_special]
  LED8 = LED - 5mm [color="Yellow (592nm)" package="5 mm [THT]"]
  LED9 = LED - 5mm [color="Red (633nm)" package="5 mm [THT]"]
  LED10 = LED - 5mm [color="Green (565nm)" package="5 mm [THT]"]
  R16 = Resistor [tolerance=±5% resistance=680 package=THT]
  R17 = Resistor [tolerance=±5% resistance=680 package=THT]
  R18 = Resistor [tolerance=±5% resistance=680 package=THT]
  S7 = Taiway 100-SP-X-T1 SPDT Miniature Toggle Switch [part_number=100-SP-X-T1-0-0-B1-M2 package=THT]
  WeMos_D1_Mini_Relay_Shield3 = WeMos D1 Mini Relay Shield  # not connected
  WeMos_D1_Mini_Relay_Shield4 = WeMos D1 Mini Relay Shield

nets:
  N1: Raspberry_Pi2.3V3, R7.Pin_1
  3V3: Raspberry_Pi2.5V, WeMos_D1_Mini_Relay_Shield1.3V3, WeMos_D1_Mini_Relay_Shield2.3V3
  N2: Raspberry_Pi2.GND, LED5.cathode, LED7.cathode, WeMos_D1_Mini_Relay_Shield1.RST, S6.COM, LED6.cathode, WeMos_D1_Mini_Relay_Shield2.RST
  N3: Raspberry_Pi2.GPIO_23, R11.Pin_0
  N4: Raspberry_Pi2.GPIO_17, S6.L1
  N5: Raspberry_Pi2.GPIO_18, S6.L2
  N6: Raspberry_Pi2.GPIO_27, WeMos_D1_Mini_Relay_Shield2.D7
  N7: Raspberry_Pi2.GPIO_22, R15.Pin_0
  N8: Raspberry_Pi2.GPIO_4, WeMos_D1_Mini_Relay_Shield1.D7
  N9: Part3.GND, Part3.SIG
  N10: LED5.anode, R15.Pin_1
  N11: LED7.anode, R7.Pin_0
  N12: WeMos_D1_Mini_Relay_Shield1.COM, BAT3.V+, WeMos_D1_Mini_Relay_Shield2.COM
  N13: WeMos_D1_Mini_Relay_Shield1.NO, M2.pin_1, WeMos_D1_Mini_Relay_Shield2.NO
  N14: BAT3.V-, M2.pin_2
  N15: R11.Pin_1, LED6.anode
  N16: U1.1, R16.Pin_0
  N17: U1.2, WeMos_D1_Mini_Relay_Shield4.A0, WeMos_D1_Mini_Relay_Shield4.RX
  3V3_2: U1.6, LED8.cathode, LED9.cathode, LED10.cathode, S7.COM, WeMos_D1_Mini_Relay_Shield4.3V3, WeMos_D1_Mini_Relay_Shield4.5V
  N18: U1.7, WeMos_D1_Mini_Relay_Shield4.RST
  N19: U1.11, S7.L1
  N20: U1.12, S7.L2
  N21: U1.13, WeMos_D1_Mini_Relay_Shield4.TX
  N22: U1.15, R18.Pin_1
  N23: U1.16, R17.Pin_0
  N24: LED8.anode, R17.Pin_1
  N25: LED9.anode, R16.Pin_1
  N26: LED10.anode, R18.Pin_0
